# Fritzing sketch 6v (saved by Fritzing 0.9.3b)
circuit board: 8.46667cm x 5.64444cm
breadboards: 1

parts:
  V1 = AC Power [voltage=5 frequency=60]
  R1 = Resistor [tolerance=±5% resistance=220 package=THT]
  Z1 = VARISTOR [package=0603-res]
  C1 = Electrolytic Capacitor [capacitance=1µF package="100 mil [THT, electrolytic]"]
  D1 = Rectifier Diode [package="Melf DO-213 AA [SMD]"]  # not connected
  D2 = Rectifier Diode [package="Melf DO-213 AA [SMD]"]
  D3 = Rectifier Diode [package="Melf DO-213 AA [SMD]"]  # not connected
  r31k = Resistor [tolerance=±5% resistance=220 package=THT]
  R2 = Resistor [tolerance=±5% resistance=100 package=THT]
  C2 = Capacitor [package=grm43d]
  D5 = Zener Diode [part_number=1N4732A breakdown_voltage=3.6V package="300 mil [THT]"]
  LED1 = LEDs [package=fkit-led-1206]
  R3 = Resistor [tolerance=±5% resistance=220 package=THT]
  F1 = Resettable Fuse PTC [package=ptc]
  D6 = Rectifier Diode [package="Melf DO-213 AA [SMD]"]

nets:
  N1: V1.V+, F1.1
  N2: V1.V-, R2.Pin_0
  N3: R1.Pin_0, C1.-, D5.anode, LED1.A, LED1.C, D6.anode
  N4: R1.Pin_1, D5.cathode, R3.Pin_1
  N5: Z1.1, R2.Pin_1, D6.cathode
  N6: Z1.2, F1.2
  N7: C1.+, D2.cathode, r31k.Pin_1, C2.1, R3.Pin_0
  N8: r31k.Pin_0, C2.2
